# Fritzing sketch Spaduino (saved by Fritzing 0.9.3b)
breadboards: 1

parts:
  U1 = atmega168 [package=dip]
  R1 = Resistor [tolerance=±5% resistance=10k package=THT]
  R2 = Resistor [tolerance=±5% resistance=6.8k package=THT]
  R3 = Resistor [tolerance=±5% resistance=6.8k package=THT]
  U2 = Voltage Regulator - 5V [part_number=7805 package="TO220 [THT]"]
  R4 = Resistor [tolerance=±5% resistance=1k package=THT]
  LED1 = LED - 3mm [color="Red (633nm)" package="3 mm [THT]"]
  C1 = Ceramic Capacitor [capacitance=100nF package="100 mil [THT, multilayer]"]
  C2 = Ceramic Capacitor [capacitance=100nF package="100 mil [THT, multilayer]"]
  C3 = Electrolytic Capacitor [capacitance=1µF package="100 mil [THT, electrolytic]"]
  R5 = Resistor [tolerance=±5% resistance=220 package=THT]

nets:
  N1: U1.RESET, R1.Pin_1
  N2: U1.D4, R5.Pin_1
  N3: U1.VCC, U1.AVCC, R1.Pin_0, R2.Pin_1, R3.Pin_1, U2.output_voltage, C1.1, C2.1, C3.+
  GND: U1.GND, U2.GND, LED1.cathode, C1.0, C2.0, C3.-
  N4: U1.D11_(PWM), R4.Pin_0
  N5: U1.A4, R3.Pin_0
  N6: U1.A5, R2.Pin_0
  N7: R4.Pin_1, LED1.anode

notes:
  Pin 1
  Pin 4
  Pin 5
  Pin 6
  Pin 8
  SDA
  SCL
